// Logisim project 4BitBinaryToDeneryConverter.circ as structural Verilog: 1 circuit, main circuit main
module main (
  input  in_1,
  input  in_2,
  input  in_3,
  input  in_4,
  output out_5,
  output out_6,
  output out_7,
  output out_8,
  output out_9,
  output out_10,
  output out_11,
  output out_12,
  output out_13,
  output out_14,
  output out_15,
  output out_16,
  output out_17,
  output out_18,
  output out_19,
  output out_20
);

  wire not_1_out, not_2_out, not_3_out, not_4_out, not_5_out, not_6_out, not_7_out, not_8_out, not_9_out,
       not_10_out, not_11_out, not_12_out, not_13_out, not_14_out, not_15_out, not_16_out, not_17_out,
       not_18_out, not_19_out, not_20_out, not_21_out, not_22_out, not_23_out, not_24_out, not_25_out,
       not_26_out, not_27_out, not_28_out, not_29_out, not_30_out, not_31_out, not_32_out;

  and and_1 (out_5, not_2_out, not_1_out, not_5_out, not_6_out);
  not not_1 (not_1_out, in_3);
  not not_2 (not_2_out, in_4);
  and and_2 (out_6, in_4, not_7_out, not_4_out, not_3_out);
  not not_3 (not_3_out, in_1);
  not not_4 (not_4_out, in_2);
  not not_5 (not_5_out, in_2);
  not not_6 (not_6_out, in_1);
  not not_7 (not_7_out, in_3);
  and and_3 (out_7, not_10_out, in_3, not_8_out, not_9_out);
  not not_8 (not_8_out, in_2);
  not not_9 (not_9_out, in_1);
  not not_10 (not_10_out, in_4);
  and and_4 (out_8, in_4, in_3, not_11_out, not_14_out);
  and and_5 (out_9, not_12_out, not_13_out, in_2, not_15_out);
  not not_11 (not_11_out, in_2);
  not not_12 (not_12_out, in_4);
  not not_13 (not_13_out, in_3);
  not not_14 (not_14_out, in_1);
  and and_6 (out_10, in_4, not_16_out, in_2, not_17_out);
  not not_15 (not_15_out, in_1);
  not not_16 (not_16_out, in_3);
  not not_17 (not_17_out, in_1);
  and and_7 (out_11, not_19_out, in_3, in_2, not_18_out);
  not not_18 (not_18_out, in_1);
  not not_19 (not_19_out, in_4);
  and and_8 (out_13, not_21_out, not_22_out, not_23_out, in_1);
  and and_9 (out_12, in_4, in_3, in_2, not_20_out);
  not not_20 (not_20_out, in_1);
  not not_21 (not_21_out, in_4);
  not not_22 (not_22_out, in_3);
  and and_10 (out_14, in_4, not_24_out, not_25_out, in_1);
  not not_23 (not_23_out, in_2);
  not not_24 (not_24_out, in_3);
  not not_25 (not_25_out, in_2);
  and and_11 (out_15, not_26_out, in_3, not_27_out, in_1);
  not not_26 (not_26_out, in_4);
  not not_27 (not_27_out, in_2);
  and and_12 (out_16, in_4, in_3, not_30_out, in_1);
  and and_13 (out_17, not_28_out, not_29_out, in_2, in_1);
  not not_28 (not_28_out, in_4);
  not not_29 (not_29_out, in_3);
  not not_30 (not_30_out, in_2);
  and and_14 (out_18, in_4, not_31_out, in_2, in_1);
  not not_31 (not_31_out, in_3);
  and and_15 (out_19, not_32_out, in_3, in_2, in_1);
  not not_32 (not_32_out, in_4);
  and and_16 (out_20, in_4, in_3, in_2, in_1);
endmodule
